# Fritzing sketch FritzingSketch (saved by Fritzing 0.9.3b)
breadboards: 3

parts:
  Part1 = Arduino Uno (Rev3)
  J1 = Piezo Speaker
  DFRobot_DFPlayer_Mini1 = DFRobot DFPlayer Mini [part_number=DFR0299]
  SP1 = SPEAKER [package=pcb_mount_speaker]
  R1 = Resistor [tolerance=±5% resistance=1k package=THT]
  U1 = 7-SEGMENT-DISPLAY [package=7-segment-display]
  U2 = 7-SEGMENT-DISPLAY [package=7-segment-display]
  U3 = 74HC595 [package="DIP16 [THT]"]
  U4 = 74HC595 [package="DIP16 [THT]"]
  S2 = Pushbutton [package="[THT]"]
  S5 = Pushbutton [package="[THT]"]
  LED3 = LED - 5mm [color="Blue (430nm)" package="5 mm [THT]"]
  LED4 = LED - 5mm [color="Green (555nm)" package="5 mm [THT]"]
  S6 = Pushbutton [package="[THT]"]
  S7 = Pushbutton [package="[THT]"]
  LED5 = LED - 5mm [color="Red (635nm)" package="5 mm [THT]"]
  LED6 = LED - 5mm [color="Blue (525nm)" package="5 mm [THT]"]
  S8 = Pushbutton [package="[THT]"]
  S9 = Pushbutton [package="[THT]"]
  LED7 = LED - 5mm [color="Green (570nm)" package="5 mm [THT]"]
  LED8 = LED - 5mm [color="Yellow (595nm)" package="5 mm [THT]"]
  S10 = Pushbutton [package="[THT]"]
  LED9 = LED - 5mm [color="Orange (620nm)" package="5 mm [THT]"]
  U5 = 74HC595 [package="DIP16 [THT]"]

nets:
  N1: Part1.A0, U3.DS, U4.Q7', U4.DS
  N2: Part1.A1, U3.ST_CP, U4.ST_CP
  N3: Part1.A2, U3.SH_CP, U4.SH_CP
  N4: Part1.A3, U5.DS
  N5: Part1.A4/SDA, U5.ST_CP
  N6: Part1.A5/SCL, U5.SH_CP
  N7: Part1.D11_PWM/MOSI, J1.pin2
  N8: Part1.D12/MISO, R1.Pin_1
  N9: Part1.D13/SCK, DFRobot_DFPlayer_Mini1.DAC_R
  GND: Part1.GND, Part1.D0/RX, Part1.D1/TX, Part1.D2, Part1.D3_PWM, Part1.D4, Part1.D5_PWM, Part1.D6_PWM, J1.pin1, DFRobot_DFPlayer_Mini1.GND-1, DFRobot_DFPlayer_Mini1.GND-2, U3.GND, U3.OE, U4.GND, U4.OE, S2.Pin_1, S2.Pin_2, S2.Pin_3, S2.Pin_4, S5.Pin_1, S5.Pin_2, S5.Pin_3, S5.Pin_4, LED3.cathode, LED4.cathode, S6.Pin_1, S6.Pin_2, S6.Pin_3, S6.Pin_4, S7.Pin_1, S7.Pin_2, S7.Pin_3, S7.Pin_4, LED5.cathode, LED6.cathode, S8.Pin_1, S8.Pin_2, S8.Pin_3, S8.Pin_4, S9.Pin_1, S9.Pin_2, S9.Pin_3, S9.Pin_4, LED7.cathode, LED8.cathode, S10.Pin_1, S10.Pin_2, S10.Pin_3, S10.Pin_4, LED9.cathode, U5.GND, U5.OE
  VCC: Part1.5V, DFRobot_DFPlayer_Mini1.VCC, U1.F, U2.F, U3.MR, U3.VCC, U4.MR, U4.VCC, U5.VCC
  N10: DFRobot_DFPlayer_Mini1.RX, R1.Pin_0
  N11: DFRobot_DFPlayer_Mini1.SPK_1, SP1.-
  N12: DFRobot_DFPlayer_Mini1.SPK_2, SP1.+
  N13: U1.E, U3.Q5
  N14: U1.D, U3.Q2
  N15: U1.G1, U3.Q3
  N16: U1.DP, U3.Q4
  N17: U1.A, U3.Q1
  N18: U1.G2, U3.Q0
  N19: U1.G, U3.Q6
  N20: U2.E, U4.Q5
  N21: U2.D, U4.Q4
  N22: U2.G1, U4.Q3
  N23: U2.DP, U4.Q2
  N24: U2.A, U4.Q1
  N25: U2.G2, U4.Q0
  N26: U2.G, U4.Q6
  N27: LED3.anode, U5.Q6
  N28: LED4.anode, U5.Q5
  N29: LED5.anode, U5.Q4
  N30: LED6.anode, U5.Q3
  N31: LED7.anode, U5.Q2
  N32: LED8.anode, U5.Q1
  N33: LED9.anode, U5.Q0
